// Logisim project risc_cpu_simulation.circ as structural Verilog: 5 circuits, main circuit main
module main (
  input  in_1,
  input  in_2,
  output [31:0] out_3,
  output [31:0] out_4
);

  wire [31:0] i_memory_1_instr, pc_v1_1_pc_out, register_1_q;

  Register #(.width(32)) register_1 (.D(pc_v1_1_pc_out), .en(1'b1), .clk(in_1), .Q(register_1_q), .clr(in_2));
  PC_v1 pc_v1_1 (.Clk(in_1), .Reset(in_2), .PC_Out(pc_v1_1_pc_out));  // open: PC_In, PC_Select
  I_Memory i_memory_1 (.Addr(pc_v1_1_pc_out), .Clk(in_1), .Reset(in_2), .Instr(i_memory_1_instr));  // open: Stall
  IF_ID_Reg if_id_reg_1 (
    .PC_In(register_1_q), .Instr_In(i_memory_1_instr), .WE(1'b1), .Clk(in_1), .Reset(in_2), .PC_Out(out_3),
    .Instr_Out(out_4));
endmodule

module PC_v1 (
  input  [31:0] PC_In,
  input  PC_Select,
  input  Clk,
  input  Reset,
  output [31:0] PC_Out
);

  wire [31:0] adder_1_out, multiplexer_1_out;

  Adder #(.width(32)) adder_1 (.a(PC_Out), .b(32'h4), .out(adder_1_out));  // open: cin, cout
  Multiplexer #(.width(32)) multiplexer_1 (.in0(adder_1_out), .in1(PC_In), .out(multiplexer_1_out), .sel(PC_Select));
  Register #(.width(32)) register_1 (.D(multiplexer_1_out), .en(1'b1), .clk(Clk), .Q(PC_Out), .clr(Reset));
endmodule

module I_Memory (
  input  [31:0] Addr,
  input  Clk,
  input  Reset,
  output [31:0] Instr,
  output Stall
);

  wire [31:0] register_1_q;

  Register #(.width(32)) register_1 (.D(Addr), .en(1'b1), .clk(Clk), .Q(register_1_q), .clr(Reset));
  ROM #(.addrWidth(16), .dataWidth(32)) rom_1 (.addr(register_1_q[17:2]), .data(Instr));

  assign Stall = 1'b0;
endmodule

module Instr_Reg (
  input  [31:0] D,
  input  WE,
  input  Clk,
  input  Reset,
  output [31:0] Q
);

  wire and_1_out, and_2_out, and_3_out, and_4_out, and_5_out, and_6_out, and_7_out, and_8_out, and_9_out,
       and_10_out, or_1_out, or_2_out, or_3_out, or_4_out, or_5_out;

  and and_1 (and_1_out, D[4], WE);
  and and_2 (and_2_out, ~WE, Q[4]);  // AND_Gate
  and and_3 (and_3_out, D[3], WE);
  and and_4 (and_4_out, ~WE, Q[3]);  // AND_Gate
  and and_5 (and_5_out, D[2], WE);
  and and_6 (and_6_out, ~WE, Q[2]);  // AND_Gate
  and and_7 (and_7_out, D[1], WE);
  and and_8 (and_8_out, ~WE, Q[1]);  // AND_Gate
  and and_9 (and_9_out, D[0], WE);
  and and_10 (and_10_out, ~WE, Q[0]);  // AND_Gate
  Register #(.width(27)) register_1 (.D(D[31:5]), .en(WE), .clk(Clk), .Q(Q[31:5]), .clr(Reset));
  D_Flip_Flop d_ff_1 (.D(or_1_out), .clk(Clk), .Q(Q[4]), .preset(Reset));  // open: Qn, reset
  or or_1 (or_1_out, and_1_out, and_2_out);
  D_Flip_Flop d_ff_2 (.D(or_2_out), .clk(Clk), .Q(Q[3]), .reset(Reset));  // open: Qn, preset
  or or_2 (or_2_out, and_3_out, and_4_out);
  D_Flip_Flop d_ff_3 (.D(or_3_out), .clk(Clk), .Q(Q[2]), .reset(Reset));  // open: Qn, preset
  or or_3 (or_3_out, and_5_out, and_6_out);
  D_Flip_Flop d_ff_4 (.D(or_4_out), .clk(Clk), .Q(Q[1]), .preset(Reset));  // open: Qn, reset
  or or_4 (or_4_out, and_7_out, and_8_out);
  D_Flip_Flop d_ff_5 (.D(or_5_out), .clk(Clk), .Q(Q[0]), .preset(Reset));  // open: Qn, reset
  or or_5 (or_5_out, and_9_out, and_10_out);
  // Probe on Q
endmodule

module IF_ID_Reg (
  input  [31:0] PC_In,
  input  [31:0] Instr_In,
  input  WE,
  input  Clk,
  input  Reset,
  output [31:0] PC_Out,
  output [31:0] Instr_Out
);

  wire not_1_out;

  Register #(.trigger("falling"), .width(32)) PC (.D(PC_In), .en(WE), .clk(Clk), .Q(PC_Out), .clr(Reset));
  Instr_Reg Instr (.WE(WE), .Clk(not_1_out), .Reset(Reset), .D(Instr_In), .Q(Instr_Out));
  not not_1 (not_1_out, Clk);
endmodule
